# Fritzing sketch WiringDiagram (saved by Fritzing 0.9.2b)
breadboards: 1

parts:
  Part1 = Arduino Yun
  S1 = Momentary Switch [package=tactile-pth]
  S2 = Momentary Switch [package=tactile-pth]
  S3 = Momentary Switch [package=tactile-pth]
  R1 = Resistor [tolerance=±5% resistance=220 package="0402 [SMD]"]
  R2 = Resistor [tolerance=±5% resistance=220 package="0402 [SMD]"]
  R3 = Resistor [tolerance=±5% resistance=220 package="0402 [SMD]"]

nets:
  N1: Part1.D2/SDA, Part1.D2, S2.3, R2.Pin_1
  N2: Part1.D3/SCL, Part1.D3_PWM, S1.3, R1.Pin_1
  N3: Part1.D4, S3.3, R3.Pin_1
  N4: Part1.5V, R1.Pin_0, R2.Pin_0, R3.Pin_0
  N5: Part1.GND, S1.4, S2.4, S3.4

notes:
  VCC GND SCL SDA
  pins on the OLED display
